// Logisim project OR.circ as structural Verilog: 1 circuit, main circuit main
module main (
  input  in_1,
  input  in_2
);

  wire nand_1_out, nand_2_out, nand_3_out;

  LED led_1 (.in(nand_1_out));
  nand nand_1 (nand_1_out, in_1, in_1);
  nand nand_2 (nand_2_out, in_2, in_2);
  LED led_2 (.in(nand_2_out));
  nand nand_3 (nand_3_out, nand_1_out, nand_2_out);
  LED led_3 (.in(nand_3_out));
endmodule
